# Fritzing sketch HcSr04 (saved by Fritzing 0.9.6b)

parts:
  HC-SR04_Sensor_1 = HC-SR04 Ultrasonic Distance Sensor
  Raspberry_Pi_1 = Raspberry Pi 4B

nets:
  VCC: HC-SR04_Sensor_1.VCC, Raspberry_Pi_1.5V
  N1: HC-SR04_Sensor_1.TRIG, Raspberry_Pi_1.GPIO25
  N2: HC-SR04_Sensor_1.ECHO, Raspberry_Pi_1.GPIO24
  GND: HC-SR04_Sensor_1.GND, Raspberry_Pi_1.GND
